// Logisim project Regfile.circ as structural Verilog: 2 circuits, main circuit main
module main (
  input  [1:0] Read_register_1,
  input  [1:0] Read_register_2,
  input  [1:0] write_register,
  input  [15:0] write_data,
  input  RegWrite,
  input  clock,
  output [15:0] Reg_0_Value,
  output [15:0] Reg_1_Value,
  output [15:0] Reg_2_Value,
  output [15:0] Reg_3_Value,
  output [15:0] Read_Data_1,
  output [15:0] Read_Data_2
);

  wire _0, _1, _2, _3;

  Demultiplexer #(.select(2)) demultiplexer_1 (
    .out0(_0), .out1(_1), .out2(_2), .out3(_3), .in(RegWrite), .sel(write_register));  // open: en
  Register #(.width(16)) register_1 (.D(write_data), .en(_0), .Q(Reg_0_Value), .clk(clock));  // open: clr
  Register #(.width(16)) register_2 (.D(write_data), .en(_1), .Q(Reg_1_Value), .clk(clock));  // open: clr
  Register #(.width(16)) register_3 (.D(write_data), .en(_2), .Q(Reg_2_Value), .clk(clock));  // open: clr
  Register #(.width(16)) register_4 (.D(write_data), .en(_3), .Q(Reg_3_Value), .clk(clock));  // open: clr
  Multiplexer #(.select(2), .width(16)) multiplexer_1 (
    .in0(Reg_0_Value), .in1(Reg_1_Value), .in2(Reg_2_Value), .in3(Reg_3_Value), .out(Read_Data_1),
    .sel(Read_register_1));  // open: en
  Multiplexer #(.select(2), .width(16)) multiplexer_2 (
    .in0(Reg_0_Value), .in1(Reg_1_Value), .in2(Reg_2_Value), .in3(Reg_3_Value), .out(Read_Data_2),
    .sel(Read_register_2));  // open: en

  // Other names for the same wires on the sheet: R1[1:0] = Read_register_1; R2[1:0] = Read_register_2;
  //   wr[1:0] = write_register

  // Notes on the sheet:
  //   These are INPUTS to the circuit
  //   These are INPUTS to the circuit
  //   Register 0
  //   Register 1
  //   Register 2
  //   Register 3
  //   DO NOT CHANGE THE LOCATIONS OF THE INPUTS/OUTPUTS! IF YOU DO SO, YOU NEED TO MAKE SURE THE PINS ARE AT THE RIGHT PLACE!
  //   These are OUTPUTS to the circuit
  //   Yet again, the clock is not an actual clock, but an input, one that will should/will be inputed from the higher circuit
  //   These are OUTPUTS to the circuit
endmodule

module _4_1 (
  output [15:0] out_1,
  output [15:0] out_2
);
endmodule
