// Logisim project alu.circ as structural Verilog: 3 circuits, main circuit main
module main (
  input  [15:0] X,
  input  [15:0] Y,
  input  [3:0] switch__S,
  output signed_overflow,
  output [15:0] result,
  output equal
);

  wire add_overflow_1_out, comparator_1_lt, comparator_2_eq, comparator_3_eq, O1, O2, or_2_out,
       sub_overflow_1_out;
  wire [3:0] bitadder_2_out, bitadder_3_out, bitfinder_1_index, subtractor_2_out;
  wire [4:0] bitadder_1_out;
  wire [15:0] _0, _1, _2, _3, _4, _5, _6, _7, _8, _9, _10;

  assign _0 = X & Y;  // AND_Gate and_1, 16 bits wide
  Comparator #(.width(16)) comparator_1 (.a(X), .b(Y), .lt(comparator_1_lt));  // open: gt, eq
  Adder #(.width(16)) adder_1 (.a(X), .b(Y), .out(_6), .cout(O1));  // open: cin
  Subtractor #(.width(16)) subtractor_1 (.a(X), .b(Y), .out(_7), .bout(O2));  // open: bin
  assign _1 = X | Y;  // OR_Gate or_1, 16 bits wide
  assign _2 = {{15{1'b0}}, comparator_1_lt};  // Bit_Extender bit_extender_1
  Shifter #(.width(16)) shifter_1 (.in(X), .\dist (Y[3:0]), .out(_3));
  Shifter #(.width(16), .shift("lr")) shifter_2 (.in(X), .\dist (Y[3:0]), .out(_4));
  Shifter #(.width(16), .shift("ar")) shifter_3 (.in(X), .\dist (Y[3:0]), .out(_5));
  BitFinder #(.width(16), .\type ("high1")) bitfinder_1 (.in(X), .index(bitfinder_1_index));  // open: found
  BitAdder #(.width(16)) bitadder_1 (.in0(X), .out(bitadder_1_out));
  Subtractor #(.width(4)) subtractor_2 (.a(4'b1111), .b(bitfinder_1_index), .out(subtractor_2_out));  // open: bin, bout
  assign _10 = {{11{1'b0}}, bitadder_1_out};  // Bit_Extender bit_extender_2
  Multiplexer #(.select(4), .width(16)) multiplexer_1 (
    .in0(_0), .in1(_1), .in2(_2), .in3(_3), .in4(_4), .in5(_5), .in6(_6), .in7(_7), .in8(_8), .in9(_9),
    .in10(_10), .out(result), .sel(switch__S));  // open: in11, in12, in13, in14, in15, en
  assign _8 = {{12{1'b0}}, subtractor_2_out};  // Bit_Extender bit_extender_3
  BitAdder bitadder_2 (.in0(X[7:0]), .out(bitadder_2_out));
  BitAdder bitadder_3 (.in0(X[15:8]), .out(bitadder_3_out));
  add_overflow add_overflow_1 (.Result(result), .X(X), .Y(Y), .out(add_overflow_1_out));
  sub_overflow sub_overflow_1 (.X(X), .Y(Y), .Result(result), .out(sub_overflow_1_out));
  Comparator #(.width(4)) comparator_2 (.a(4'b0000), .b(bitadder_2_out), .eq(comparator_2_eq));  // open: gt, lt
  Comparator #(.width(4)) comparator_3 (.a(bitadder_3_out), .b(4'b0000), .eq(comparator_3_eq));  // open: gt, lt
  or or_2 (or_2_out, comparator_2_eq, comparator_3_eq);
  assign _9 = {{15{1'b0}}, or_2_out};  // Bit_Extender bit_extender_4
  Multiplexer #(.select(4)) multiplexer_2 (
    .in0(1'b0), .in1(1'b0), .in2(1'b0), .in3(1'b0), .in4(1'b0), .in5(1'b0), .in6(add_overflow_1_out),
    .in7(sub_overflow_1_out), .out(signed_overflow), .sel(switch__S));  // open: in8, in9, in10, in11, in12, in13, in14, in15, en
  Comparator #(.width(16)) comparator_4 (.a(X), .b(Y), .eq(equal));  // open: gt, lt

  // Other names for the same wires on the sheet: Select[3:0] = switch__S

  // Notes on the sheet:
  //   These are INPUTS to your circuit
  //   This is an INPUT to your circuit
  //   DO NOT CHANGE THE LOCATIONS OF THE INPUTS/OUTPUTS! IF YOU DO SO, YOU NEED TO MAKE SURE THE PINS ARE AT THE RIGHT PLACE!
  //   These are OUTPUTS to your circuit
endmodule

module add_overflow (
  input  [15:0] Result,
  input  [15:0] X,
  input  [15:0] Y,
  output out
);

  wire and_1_out, comparator_1_eq, comparator_2_eq, not_1_out;

  and and_1 (and_1_out, X[15], Y[15]);
  Comparator #(.width(1)) comparator_1 (.a(Result[15]), .b(and_1_out), .eq(comparator_1_eq));  // open: gt, lt
  Comparator #(.width(1)) comparator_2 (.a(X[15]), .b(Y[15]), .eq(comparator_2_eq));  // open: gt, lt
  not not_1 (not_1_out, comparator_1_eq);
  and and_2 (out, not_1_out, comparator_2_eq);
endmodule

module sub_overflow (
  input  [15:0] X,
  input  [15:0] Y,
  input  [15:0] Result,
  output out
);

  wire and_1_out, comparator_1_eq, xor_1_out;

  xor xor_1 (xor_1_out, X[15], Y[15]);
  and and_1 (and_1_out, Result[15], X[15]);
  Comparator #(.width(1)) comparator_1 (.a(xor_1_out), .b(and_1_out), .eq(comparator_1_eq));  // open: gt, lt
  not not_1 (out, comparator_1_eq);

  // Notes on the sheet:
  //   ALMOST THERE. THE ORDER OF THE INPUTS MATTER. THE RESULT SHOULD BE THE SAME AS THE X INPUT
endmodule
