// Logisim project cpu.circ as structural Verilog: 16 circuits, main circuit main
// Main circuit
module main (
  input  [15:0] From_Instr_Mem,
  input  clk,
  output [15:0] r0,
  output [15:0] r1,
  output [15:0] r2,
  output [15:0] r3,
  output [15:0] Display_0,
  output [15:0] Display_1,
  output [15:0] To_Instr_Mem,
  output [15:0] Data_Mem_Data,
  output [15:0] Data_Mem_Addr,
  output Data_Mem_Write
);

  wire Branch_Select, button_1_out, comparator_1_eq, data_write_1_write_bacj, extend_selec_1_select,
       func_or_10_1_rs_rt_select, Func_Select, main_1_signed_overflow, Mem_choose_2, Mem_Chooser, No_Op,
       not_2_out, opcode_func_or_branch_1_func_select, opcode_reader_1_out_2, undriven;
  wire [1:0] RD, register_picker_1_read_1, register_picker_1_read_2, register_picker_1_write, RS_1, RS_2,
       rs_rt_rd_1_rs, rs_rt_rd_1_rt, RT_1, RT_2;
  wire [3:0] Funct, Imm_func, multiplexer_3_out;
  wire [5:4] demultiplexer_1_out1;
  wire [7:0] Immediate;
  wire [11:0] demultiplexer_1_out0, demultiplexer_2_out1;
  wire [15:0] data_write_1_write_data, extender_1_out_3, Inst_2, multiplexer_1_out, multiplexer_4_out, rt,
       Write_Data_1, Write_Data_2, X1, Y1;

  extend_selec extend_selec_1 (.opcode(Inst_2[15:12]), .select(extend_selec_1_select));
  func_or_10 func_or_10_1 (.func_select(Func_Select), .opcode(Inst_2[15:12]), .rs_rt_select(func_or_10_1_rs_rt_select));
  Extender extender_1 (.Immediate(Immediate), .select(extend_selec_1_select), .out_3(extender_1_out_3));
  // Probe on Inst_2
  immediate_functions immediate_functions_1 (.Opcode(Inst_2[15:12]), .Funct(Imm_func));
  rs_rt_rd rs_rt_rd_1 (
    .RS_1(RS_1), .RT_1(RT_1), .RS_2(RS_2), .RT_2(RT_2), .select(func_or_10_1_rs_rt_select),
    .RS(rs_rt_rd_1_rs), .RT(rs_rt_rd_1_rt));
  Register_Picker register_picker_1 (
    .opcode(Inst_2[15:12]), .RS(rs_rt_rd_1_rs), .RT(rs_rt_rd_1_rt), .RD(RD),
    .Read_1(register_picker_1_read_1), .Read_2(register_picker_1_read_2), .Write(register_picker_1_write));
  Data_Write data_write_1 (
    .Opcode(Inst_2[15:12]), .Data_1(Write_Data_1), .Data_2(Write_Data_2), .Data_Write(Data_Mem_Data),
    .Immediate(Immediate), .Write_Data(data_write_1_write_data), .Write_Bacj(data_write_1_write_bacj));
  opcode_func_or_branch opcode_func_or_branch_1 (
    .Opcode(Inst_2[15:12]), .func_select(opcode_func_or_branch_1_func_select));
  Regfile_main Register (
    .Read_register_1(register_picker_1_read_1), .Read_register_2(register_picker_1_read_2),
    .write_register(register_picker_1_write), .write_data(data_write_1_write_data), .Reg_0_Value(r0),
    .Reg_1_Value(r1), .Reg_2_Value(r2), .Reg_3_Value(r3), .RegWrite(data_write_1_write_bacj), .clock(clk),
    .Read_Data_1(X1), .Read_Data_2(rt));
  not not_1 (Func_Select, opcode_func_or_branch_1_func_select);
  Comparator #(.width(4), .mode("unsigned")) comparator_1 (
    .a(4'b0000), .b(Inst_2[15:12]), .eq(comparator_1_eq));  // open: gt, lt
  Demultiplexer #(.width(12), .enable("false")) demultiplexer_1 (
    .out0(demultiplexer_1_out0), .out1({RS_1, RT_1, RD, demultiplexer_1_out1, Funct}), .in(Inst_2[11:0]),
    .sel(comparator_1_eq));
  Multiplexer #(.width(16)) multiplexer_1 (
    .in0(From_Instr_Mem), .in1({16{1'b0}}), .out(multiplexer_1_out), .sel(No_Op));  // open: en
  Multiplexer #(.width(16)) multiplexer_2 (.in0(rt), .in1(extender_1_out_3), .out(Y1), .sel(Func_Select));  // open: en
  Opcode_Reader opcode_reader_1 (.opcode(Inst_2[15:12]), .out_2(opcode_reader_1_out_2));
  Register #(.width(16)) register_2 (.D(multiplexer_1_out), .Q(Inst_2), .clk(clk));  // open: en, clr
  Demultiplexer #(.width(12), .enable("false")) demultiplexer_2 (
    .out0({RS_2, RT_2, Immediate}), .out1(demultiplexer_2_out1), .in(demultiplexer_1_out0),
    .sel(opcode_reader_1_out_2));
  Multiplexer #(.width(4)) multiplexer_3 (
    .in0(Funct), .in1(Imm_func), .out(multiplexer_3_out), .sel(Func_Select));  // open: en
  PC_Choose pc_choose_1 (
    .Immediate(Immediate), .clk(clk), .Input(demultiplexer_2_out1), .opcode(Inst_2[15:12]),
    .Branch_Select(Branch_Select), .no_op(No_Op), .Rs(X1), .R3(Write_Data_1), .Next_Address(To_Instr_Mem));  // open: out_7
  alu_main main_1 (
    .switch__S(multiplexer_3_out), .X(X1), .equal(Branch_Select), .result(Write_Data_2),
    .signed_overflow(main_1_signed_overflow), .Y(Y1));
  LED led_1 (.in(main_1_signed_overflow));
  Multiplexer #(.width(16)) multiplexer_4 (
    .in0({16{1'b0}}), .in1(rt), .out(multiplexer_4_out), .sel(Mem_Chooser));  // open: en
  Hex_Digit_Display hex_digit_display_1 (.value(Display_0[15:12]));  // open: dp
  Hex_Digit_Display hex_digit_display_2 (.value(Display_0[11:8]));  // open: dp
  Multiplexer #(.width(16)) multiplexer_5 (
    .in0({16{1'b0}}), .in1(Write_Data_2), .out(Data_Mem_Addr), .sel(Mem_Chooser));  // open: en
  Hex_Digit_Display hex_digit_display_3 (.value(Display_0[3:0]), .dp(undriven));
  Hex_Digit_Display hex_digit_display_4 (.value(Display_0[7:4]));  // open: dp
  assign Data_Mem_Data = Data_Mem_Write ? multiplexer_4_out : 16'bz;  // Controlled_Buffer controlled_buffer_1
  Hex_Digit_Display hex_digit_display_5 (.value(Display_1[15:12]));  // open: dp
  Button button_1 (.out(button_1_out));
  not not_2 (not_2_out, Data_Mem_Write);
  Hex_Digit_Display hex_digit_display_6 (.value(Display_1[7:4]));  // open: dp
  Hex_Digit_Display hex_digit_display_7 (.value(Display_1[11:8]));  // open: dp
  RAM #(.addrWidth(16), .dataWidth(16)) ram_1 (
    .addr(Data_Mem_Addr), .data(Data_Mem_Data), .sel(1'b1), .clk(clk), .ld(not_2_out), .clr(button_1_out));
  Mem_Write mem_write_1 (.Op_Code(Inst_2[15:12]), .Mem_Write(Data_Mem_Write));
  Hex_Digit_Display hex_digit_display_8 (.value(Display_1[3:0]));  // open: dp
  Mem_Chooser mem_chooser_1 (.Opcode(Inst_2[15:12]), .Select_Addr(Mem_Chooser), .Select_Data(Mem_choose_2));
  Display u_display_1 (.Rs(X1), .Opcode(Inst_2[15:12]), .Imm(Immediate), .clk(clk), .D0(Display_0), .D1(Display_1));

  // Other names for the same wires on the sheet: d0[15:0] = Display_0; d1[15:0] = Display_1;
  //   Data_Mem_Data1[15:0] = Data_Mem_Data; Data_Out[15:0] = Data_Mem_Data; Inst_1[15:0] = From_Instr_Mem;
  //   Opcode[3:0] = Inst_2[15:12]; Next_Addr[15:0] = To_Instr_Mem

  // Notes on the sheet:
  //   This is the instruction that you would receive as INPUT
  //   This is the current PC that you need to send as OUTPUT
  //   This is a CLK that is an INPUT driven from the harness.
  //   Remember, this circuit is loaded from the harness to be tested!
  //   DO NOT CHANGE THE LOCATIONS OF THE INPUTS/OUTPUTS! IF YOU DO SO, YOU NEED TO MAKE SURE THE PINS ARE AT THE RIGHT PLACE!
  //   IMplement the last 4 instructions
  //   These are OUTPUTS to the circuit
  //   POSSIBLE ERROR (YOU HAVE MULTIPLE RS)
  //   These are OUTPUTS to the circuit
endmodule

module Opcode_Reader (
  input  [3:0] opcode,
  output out_2
);

  wire comparator_1_eq, comparator_2_eq;

  Comparator #(.width(4), .mode("unsigned")) comparator_1 (
    .a(opcode), .b(4'b0111), .eq(comparator_1_eq));  // open: gt, lt
  Comparator #(.width(4), .mode("unsigned")) comparator_2 (
    .a(opcode), .b(4'b1000), .eq(comparator_2_eq));  // open: gt, lt
  or or_1 (out_2, comparator_1_eq, comparator_2_eq);
endmodule

module Register_Picker (
  input  [1:0] RS,
  input  [1:0] RT,
  input  [1:0] RD,
  input  [3:0] opcode,
  output [1:0] Read_1,
  output [1:0] Read_2,
  output [1:0] Write
);

  wire _12, comparator_2_eq, comparator_3_eq, comparator_4_eq, comparator_5_eq, or_1_out;
  wire [1:0] multiplexer_2_out;

  Comparator #(.width(4)) comparator_1 (.a(opcode), .b(4'b1100), .eq(_12));  // open: gt, lt
  Comparator #(.width(4)) comparator_2 (.a(opcode), .b(4'b0111), .eq(comparator_2_eq));  // open: gt, lt
  Comparator #(.width(4)) comparator_3 (.a(opcode), .b(4'b1011), .eq(comparator_3_eq));  // open: gt, lt
  Comparator #(.width(4)) comparator_4 (.a(opcode), .b(4'b1010), .eq(comparator_4_eq));  // open: gt, lt
  Comparator #(.width(4)) comparator_5 (.a(opcode), .b(4'b0000), .eq(comparator_5_eq));  // open: gt, lt
  or or_1 (or_1_out, _12, comparator_3_eq, comparator_4_eq, comparator_5_eq);
  Multiplexer #(.width(2)) multiplexer_1 (.in0(2'b00), .in1(RT), .out(Read_2), .sel(or_1_out));  // open: en
  Multiplexer #(.width(2)) multiplexer_2 (.in0(RT), .in1(RD), .out(multiplexer_2_out), .sel(or_1_out));  // open: en
  Multiplexer #(.width(2)) multiplexer_3 (
    .in0(multiplexer_2_out), .in1(2'b11), .out(Write), .sel(comparator_2_eq));  // open: en

  assign Read_1 = RS;
endmodule

module Immediate_Ops (
  input  [3:0] Opcode,
  input  [7:0] Immediate,
  input  [1:0] Rt,
  input  [1:0] Rs
);

  Demultiplexer #(.select(4), .width(12), .enable("false")) demultiplexer_1 (
    .in({Rs, Rt, Immediate}), .sel(Opcode));  // open: out0, out1, out2, out3, out4, out5, out6, out7, out8, out9, out10, out11, out12, out13, out14, out15
endmodule

module FFO (
  input  [11:0] value
);
endmodule

module Extender (
  input  select,
  input  [7:0] Immediate,
  output [15:0] out_3
);

  wire [15:0] bit_extender_1_out, bit_extender_2_out;

  assign bit_extender_1_out = {{8{1'b0}}, Immediate};  // Bit_Extender bit_extender_1
  assign bit_extender_2_out = {{8{Immediate[7]}}, Immediate};  // Bit_Extender bit_extender_2
  Multiplexer #(.width(16)) multiplexer_1 (
    .in0(bit_extender_1_out), .in1(bit_extender_2_out), .out(out_3), .sel(select));  // open: en
endmodule

module extend_selec (
  input  [3:0] opcode,
  output select
);

  Multiplexer #(.select(4)) multiplexer_1 (
    .in0(1'b0), .in1(1'b0), .in2(1'b0), .in3(1'b0), .in4(1'b1), .in5(1'b0), .in6(1'b0), .in7(1'b0),
    .in8(1'b0), .in9(1'b0), .in10(1'b1), .in11(1'b1), .in12(1'b1), .in13(1'b0), .in14(1'b0), .in15(1'b1),
    .out(select), .sel(opcode));  // open: en
endmodule

module PC_Choose (
  input  [3:0] opcode,
  input  Branch_Select,
  input  [7:0] Immediate,
  input  clk,
  input  [11:0] Input,
  input  [15:0] Rs,
  output [15:0] out_7,
  output [15:0] R3,
  output [15:0] Next_Address,
  output no_op
);

  wire _9_select, and_1_out, and_2_out, beq, bne, Branch_Taken_beq, Branch_Taken_bne, comparator_1_eq,
       comparator_2_eq, comparator_3_eq, comparator_4_eq, comparator_5_eq, no_op_t, not_1_out, not_4_out,
       not_5_out, or_2_out;
  wire [15:0] adder_1_out, bit_extender_1_out, branch, multiplexer_1_out;

  not not_1 (not_1_out, no_op_t);
  Adder #(.width(16)) adder_1 (.a(16'h1), .b(R3), .out(adder_1_out));  // open: cin, cout
  Multiplexer #(.width(16)) multiplexer_1 (
    .in0(adder_1_out), .in1(Next_Address), .out(multiplexer_1_out), .sel(not_1_out));  // open: en
  Register #(.width(16)) register_1 (.D(multiplexer_1_out), .Q(R3), .clk(clk));  // open: en, clr
  Comparator #(.width(4), .mode("unsigned")) comparator_1 (
    .a(opcode), .b(4'b0111), .eq(comparator_1_eq));  // open: gt, lt
  Comparator #(.width(4), .mode("unsigned")) comparator_2 (
    .a(opcode), .b(4'b1000), .eq(comparator_2_eq));  // open: gt, lt
  Comparator #(.width(4), .mode("unsigned")) comparator_3 (
    .a(opcode), .b(4'b1001), .eq(comparator_3_eq));  // open: gt, lt
  Comparator #(.width(4), .mode("unsigned")) comparator_4 (
    .a(opcode), .b(4'b1010), .eq(comparator_4_eq));  // open: gt, lt
  Comparator #(.width(4), .mode("unsigned")) comparator_5 (
    .a(opcode), .b(4'b1011), .eq(comparator_5_eq));  // open: gt, lt
  Comparator #(.width(4)) comparator_6 (.a(opcode), .b(4'b1010), .eq(beq));  // open: gt, lt
  and and_1 (and_1_out, comparator_4_eq, Branch_Taken_beq);
  and and_2 (and_2_out, Branch_Taken_bne, comparator_5_eq);
  assign bit_extender_1_out = {{8{Immediate[7]}}, Immediate};  // Bit_Extender bit_extender_1
  or or_1 (no_op, comparator_1_eq, comparator_2_eq, comparator_3_eq, and_1_out, and_2_out);
  Adder #(.width(16)) adder_2 (.a(bit_extender_1_out), .b(R3), .out(out_7));  // open: cin, cout
  not not_2 (no_op_t, no_op);
  // NOT_Gate not_3 has open pins: in=_9_select, out=open
  Comparator #(.width(4)) comparator_7 (.a(opcode), .b(4'b1001), .eq(_9_select));  // open: gt, lt
  Multiplexer #(.select(4), .width(16)) multiplexer_2 (
    .in0(R3), .in1(R3), .in2(R3), .in3(R3), .in4(R3), .in5(R3), .in6(R3), .in7({R3[15:12], Input}),
    .in8({R3[15:12], Input}), .in9(Rs), .in10(branch), .in11(branch), .in12(R3), .in13(R3), .in14(R3),
    .in15(R3), .out(Next_Address), .sel(opcode));  // open: en
  and and_3 (Branch_Taken_bne, bne, not_5_out);
  and and_4 (Branch_Taken_beq, Branch_Select, beq);
  or or_2 (or_2_out, Branch_Taken_beq, Branch_Taken_bne);
  not not_4 (not_4_out, or_2_out);
  Multiplexer #(.width(16)) multiplexer_3 (.in0(out_7), .in1(R3), .out(branch), .sel(not_4_out));  // open: en
  Comparator #(.width(4)) comparator_8 (.a(opcode), .b(4'b1011), .eq(bne));  // open: gt, lt
  not not_5 (not_5_out, Branch_Select);

  // Other names for the same wires on the sheet: jump[15:0] = {R3[15:12], Input}; next[15:0] = Next_Address;
  //   O[15:0] = R3; U6[5:0] = R3[15:10]; U4[3:0] = R3[15:12]; select = _9_select

  // Notes on the sheet:
  //   possible error. move right after adder
endmodule

module immediate_functions (
  input  [3:0] Opcode,
  output [3:0] Funct
);

  Multiplexer #(.select(4), .width(4)) multiplexer_1 (
    .in0(4'b0000), .in1(4'b1000), .in2(4'b1001), .in3(4'b1010), .in4(4'b0110), .in5(4'b0000), .in6(4'b0001),
    .in7(4'b0000), .in8(4'b0000), .in9(4'b0000), .in10(4'b0000), .in11(4'b0000), .in12(4'b0110),
    .in13(4'b0011), .in14(4'b0110), .in15(4'b0000), .out(Funct), .sel(Opcode));  // open: en
endmodule

module rs_rt_rd (
  input  select,
  input  [1:0] RS_1,
  input  [1:0] RT_1,
  input  [1:0] RS_2,
  input  [1:0] RT_2,
  output [1:0] RS,
  output [1:0] RT
);

  Multiplexer #(.width(2)) multiplexer_1 (.in0(RS_1), .in1(RS_2), .out(RS), .sel(select));  // open: en
  Multiplexer #(.width(2)) multiplexer_2 (.in0(RT_1), .in1(RT_2), .out(RT), .sel(select));  // open: en
endmodule

module Data_Write (
  input  [3:0] Opcode,
  input  [15:0] Data_1,
  input  [15:0] Data_2,
  input  [15:0] Data_Write,
  input  [7:0] Immediate,
  output [15:0] Write_Data,
  output Write_Bacj
);

  wire comparator_1_eq, comparator_2_eq, comparator_3_eq, not_1_out;
  wire [15:0] multiplexer_1_out, multiplexer_2_out;

  Comparator #(.width(4), .mode("unsigned")) comparator_1 (
    .a(Opcode), .b(4'b0111), .eq(comparator_1_eq));  // open: gt, lt
  not not_1 (not_1_out, comparator_1_eq);
  Multiplexer #(.width(16)) multiplexer_1 (
    .in0(Data_1), .in1(Data_2), .out(multiplexer_1_out), .sel(not_1_out));  // open: en
  Comparator #(.width(4), .mode("unsigned")) comparator_2 (
    .a(Opcode), .b(4'b1110), .eq(comparator_2_eq));  // open: gt, lt
  Multiplexer #(.width(16)) multiplexer_2 (
    .in0(multiplexer_1_out), .in1(Data_Write), .out(multiplexer_2_out), .sel(comparator_2_eq));  // open: en
  Multiplexer #(.select(4)) multiplexer_3 (
    .in0(1'b1), .in1(1'b1), .in2(1'b1), .in3(1'b1), .in4(1'b1), .in5(1'b1), .in6(1'b1), .in7(1'b1),
    .in8(1'b0), .in9(1'b0), .in10(1'b0), .in11(1'b0), .in12(1'b0), .in13(1'b1), .in14(1'b1), .in15(1'b0),
    .out(Write_Bacj), .sel(Opcode));  // open: en
  Comparator #(.width(4), .mode("unsigned")) comparator_3 (
    .a(Opcode), .b(4'b1101), .eq(comparator_3_eq));  // open: gt, lt
  Multiplexer #(.width(16)) multiplexer_4 (
    .in0(multiplexer_2_out), .in1({Immediate, {8{1'b0}}}), .out(Write_Data), .sel(comparator_3_eq));  // open: en
endmodule

module Mem_Write (
  input  [3:0] Op_Code,
  output Mem_Write
);

  wire comparator_1_eq;

  Comparator #(.width(4)) comparator_1 (.a(Op_Code), .b(4'b1100), .eq(comparator_1_eq));  // open: gt, lt
  Multiplexer multiplexer_1 (.in0(1'b0), .in1(1'b1), .out(Mem_Write), .sel(comparator_1_eq));  // open: en
endmodule

module Display (
  input  [7:0] Imm,
  input  [3:0] Opcode,
  input  [15:0] Rs,
  input  clk,
  output [15:0] D0,
  output [15:0] D1
);

  wire comparator_2_eq, comparator_3_eq, Enable, Enable_0, Enable_1;
  wire [15:0] demultiplexer_1_out0, demultiplexer_1_out1, multiplexer_1_out;

  Comparator #(.width(4)) comparator_1 (.a(Opcode), .b(4'b1111), .eq(Enable));  // open: gt, lt
  and and_1 (Enable_0, Enable, comparator_2_eq);
  Comparator #(.width(1)) comparator_2 (.a(1'b0), .b(Imm[0]), .eq(comparator_2_eq));  // open: gt, lt
  Multiplexer #(.width(16)) multiplexer_1 (
    .in0({16{1'b0}}), .in1(Rs), .out(multiplexer_1_out), .sel(Enable));  // open: en
  and and_2 (Enable_1, Enable, comparator_3_eq);
  Comparator #(.width(1)) comparator_3 (.a(1'b1), .b(Imm[0]), .eq(comparator_3_eq));  // open: gt, lt
  Demultiplexer #(.width(16), .enable("false")) demultiplexer_1 (
    .out0(demultiplexer_1_out0), .out1(demultiplexer_1_out1), .in(multiplexer_1_out), .sel(Imm[0]));
  Register #(.width(16)) register_1 (.D(demultiplexer_1_out0), .en(Enable_0), .Q(D0), .clk(clk));  // open: clr
  Register #(.width(16)) register_2 (.D(demultiplexer_1_out1), .en(Enable_1), .Q(D1), .clk(clk));  // open: clr

  // Other names for the same wires on the sheet: clock = clk; imm_t = Imm[0]
endmodule

module opcode_func_or_branch (
  input  [3:0] Opcode,
  output func_select
);

  wire comparator_1_eq, comparator_2_eq, comparator_3_eq;

  Comparator #(.width(4)) comparator_1 (.a(Opcode), .b(4'b0000), .eq(comparator_1_eq));  // open: gt, lt
  Comparator #(.width(4)) comparator_2 (.a(Opcode), .b(4'b1010), .eq(comparator_2_eq));  // open: gt, lt
  Comparator #(.width(4)) comparator_3 (.a(Opcode), .b(4'b1011), .eq(comparator_3_eq));  // open: gt, lt
  or or_1 (func_select, comparator_1_eq, comparator_2_eq, comparator_3_eq);
endmodule

module Mem_Chooser (
  input  [3:0] Opcode,
  output Select_Addr,
  output Select_Data
);

  wire comparator_1_eq, comparator_2_eq, comparator_3_eq, comparator_5_eq, comparator_6_eq;

  Comparator #(.width(4)) comparator_1 (.a(Opcode), .b(4'b1100), .eq(comparator_1_eq));  // open: gt, lt
  Comparator #(.width(4)) comparator_2 (.a(Opcode), .b(4'b1110), .eq(comparator_2_eq));  // open: gt, lt
  Comparator #(.width(4)) comparator_3 (.a(Opcode), .b(4'b1111), .eq(comparator_3_eq));  // open: gt, lt
  Comparator #(.width(4)) comparator_4 (.a(Opcode), .b(4'b1100), .eq(Select_Data));  // open: gt, lt
  Comparator #(.width(4)) comparator_5 (.a(Opcode), .b(4'b1110), .eq(comparator_5_eq));  // open: gt, lt
  Comparator #(.width(4)) comparator_6 (.a(Opcode), .b(4'b1111), .eq(comparator_6_eq));  // open: gt, lt
  or or_1 (Select_Addr, comparator_1_eq, comparator_2_eq, comparator_3_eq);
endmodule

module func_or_10 (
  input  func_select,
  input  [3:0] opcode,
  output rs_rt_select
);

  wire comparator_1_eq, comparator_2_eq;

  Comparator #(.width(4)) comparator_1 (.a(opcode), .b(4'b1010), .eq(comparator_1_eq));  // open: gt, lt
  Comparator #(.width(4)) comparator_2 (.a(opcode), .b(4'b1011), .eq(comparator_2_eq));  // open: gt, lt
  or or_1 (rs_rt_select, func_select, comparator_1_eq, comparator_2_eq);
endmodule
